# Fritzing sketch Project schematic (saved by Fritzing 0.9.3b)
breadboards: 2

parts:
  Part1 = Arduino Mega ADK (Rev3)
  ESP8266-1 = ESP8266-12 [part_number=ESP8266-12]
  ZS-042_RTC1 = ZS-042 RTC Module
  Part2 = MicroSD Card Module
  U2 = LCD-16X2 [package=lcd-16x2]

nets:
  N1: Part1.D21/SCL, ZS-042_RTC1.SCL
  N2: Part1.D20/SDA, ZS-042_RTC1.SDA
  N3: Part1.D17/RX2, ESP8266-1.TXD
  N4: Part1.D16/TX2, ESP8266-1.RXD
  N5: Part1.D9_PWM, U2.RS
  N6: Part1.D8_PWM, U2.E
  VCC: Part1.3V3, ESP8266-1.CH_PD, ESP8266-1.VCC, ESP8266-1.GPIO0, ESP8266-1.GPIO2, ZS-042_RTC1.VCC, Part2.VCC, U2.VDD, U2.A
  GND: Part1.GND, ESP8266-1.GPIO15, ESP8266-1.GND, ZS-042_RTC1.GND, Part2.GND, U2.VSS, U2.VO, U2.R_W, U2.K
  N7: Part1.D4_PWM, U2.DB7
  N8: Part1.D5_PWM, U2.DB6
  N9: Part1.D6_PWM, U2.DB5
  N10: Part1.D7_PWM, U2.DB4
  N11: Part1.D50/MISO, Part2.MISO
  N12: Part1.D51/MOSI, Part2.MOSI
  N13: Part1.D52/SCK, Part2.SCK
  N14: Part1.D53/SS, Part2.CS
